// Logisim project ALU.circ as structural Verilog: 1 circuit, main circuit main
module main (
  input  CS2,
  input  CS1,
  input  CS0,
  input  B4,
  input  B3,
  input  B2,
  input  B1,
  input  A4,
  input  A3,
  input  A2,
  input  A1,
  output out_12
);

  wire adder_1_cout, not_1_out, or_1_out, xnor_1_out, Y1_out, Z1_2_out, Z1_out;

  not not_1 (not_1_out, CS1);
  xnor xnor_1 (xnor_1_out, CS1, B1);
  nor Y1 (Y1_out, B1, CS1);
  and Z1 (Z1_out, xnor_1_out, CS1);
  or or_1 (or_1_out, Z1_out, A1);
  and Z1_2 (Z1_2_out, not_1_out, CS0);
  Adder #(.width(1)) adder_1 (.a(or_1_out), .b(Y1_out), .out(out_12), .cin(Z1_2_out), .cout(adder_1_cout));

  assign CS2 = CS1;
endmodule
