// Logisim project FP_Adder.circ as structural Verilog: 1 circuit, main circuit main
module main (
  input  [15:0] B,
  input  [15:0] A,
  input  [3:0] in_3,
  input  [3:0] in_4,
  input  [3:0] in_5,
  input  [3:0] in_6,
  input  [3:0] in_7,
  input  [3:0] in_8,
  output [3:0] out_9,
  output [12:0] out_10,
  output out_11,
  output [3:0] out_12,
  output [12:0] out_13,
  output out_14,
  output [12:0] out_15,
  output [3:0] out_16,
  output [11:0] out_17,
  output [3:0] out_18,
  output [11:0] out_19,
  output [15:0] out_20,
  output Overflow,
  output Underflow
);

  wire adder_5_cout, and_1_out;
  wire [3:0] adder_2_out, adder_4_out, bitfinder_1_index, multiplexer_1_out, subtractor_1_out, xor_5_out;
  wire [11:0] bit_extender_1_out, bit_extender_3_out, shifter_1_out, shifter_2_out, xor_9_out;
  wire [12:0] bit_extender_2_out, bit_extender_4_out;

  Adder #(.width(1)) adder_1 (.a(A[15]), .b(B[15]), .out(out_20[15]), .cin(out_11), .cout(out_14));
  Multiplexer #(.width(4), .enable("false")) multiplexer_1 (
    .in0(B[14:11]), .in1(A[14:11]), .out(multiplexer_1_out), .sel(out_11));
  Subtractor #(.width(4)) subtractor_1 (.a(multiplexer_1_out), .b(out_18), .out(subtractor_1_out));  // open: bin, bout
  Subtractor #(.width(4)) subtractor_2 (.a(in_5), .b(bitfinder_1_index), .out(out_18));  // open: bin, bout
  Adder #(.width(4)) adder_2 (.a(multiplexer_1_out), .b(in_6), .out(adder_2_out));  // open: cin, cout
  Multiplexer #(.width(4), .enable("false")) multiplexer_2 (
    .in0(subtractor_1_out), .in1(adder_2_out), .out(out_20[14:11]), .sel(and_1_out));
  Adder #(.width(4)) adder_3 (.a(A[14:11]), .b(out_9), .out(out_12), .cin(1'b1), .cout(out_11));
  xor xor_1 (out_9[0], 1'b1, B[11]);
  xor xor_2 (out_9[1], 1'b1, B[12]);
  xor xor_3 (out_9[2], 1'b1, B[13]);
  xor xor_4 (out_9[3], 1'b1, B[14]);
  BitFinder #(.width(12), .\type ("high1")) bitfinder_1 (.in(out_17), .index(bitfinder_1_index));  // open: found
  Shifter #(.width(12)) shifter_1 (.in(out_17), .\dist (out_18), .out(shifter_1_out));
  Comparator #(.width(4), .mode("unsigned")) comparator_1 (
    .a(out_20[14:11]), .b(in_8), .lt(Underflow));  // open: gt, eq
  assign bit_extender_1_out = {{1{1'b1}}, A[10:0]};  // Bit_Extender bit_extender_1
  xor xor_5 (xor_5_out[0], 1'b1, out_12[0]);
  xor xor_6 (xor_5_out[1], 1'b1, out_12[1]);
  xor xor_7 (xor_5_out[2], 1'b1, out_12[2]);
  xor xor_8 (xor_5_out[3], 1'b1, out_12[3]);
  Multiplexer #(.width(12), .enable("false")) multiplexer_3 (
    .in0(shifter_1_out), .in1(shifter_2_out), .out(out_19), .sel(and_1_out));
  assign bit_extender_2_out = {{1{1'b0}}, bit_extender_1_out};  // Bit_Extender bit_extender_2
  Comparator #(.width(4), .mode("unsigned")) comparator_2 (.a(in_7), .b(out_20[14:11]), .lt(Overflow));  // open: gt, eq
  Multiplexer #(.width(13), .enable("false")) multiplexer_4 (
    .in0(bit_extender_4_out), .in1(bit_extender_2_out), .out(out_10), .sel(out_11));
  Adder #(.width(4)) adder_4 (.a(xor_5_out), .b(in_3), .out(adder_4_out), .cin(1'b1));  // open: cout
  Shifter #(.width(12), .shift("lr")) shifter_2 (.in(out_17), .\dist (in_4), .out(shifter_2_out));
  Multiplexer #(.width(13), .enable("false")) multiplexer_5 (
    .in0(bit_extender_2_out), .in1(bit_extender_4_out), .out(out_13), .sel(out_11));
  Multiplexer #(.width(4), .enable("false")) multiplexer_6 (
    .in0(adder_4_out), .in1(out_12), .out(out_16), .sel(out_11));
  and and_1 (and_1_out, adder_5_cout, out_17[11]);
  Shifter #(.width(13), .shift("lr")) shifter_3 (.in(out_13), .\dist (out_16), .out(out_15));
  assign bit_extender_3_out = {{1{1'b1}}, B[10:0]};  // Bit_Extender bit_extender_3
  Adder #(.width(12)) adder_5 (.a(out_10[11:0]), .b(xor_9_out), .out(out_17), .cin(1'b1), .cout(adder_5_cout));
  assign bit_extender_4_out = {{1{1'b0}}, bit_extender_3_out};  // Bit_Extender bit_extender_4
  xor xor_9 (xor_9_out[0], out_15[0], 1'b1);
  xor xor_10 (xor_9_out[1], out_15[1], 1'b1);
  xor xor_11 (xor_9_out[2], out_15[2], 1'b1);
  xor xor_12 (xor_9_out[3], out_15[3], 1'b1);
  xor xor_13 (xor_9_out[4], out_15[4], 1'b1);
  xor xor_14 (xor_9_out[5], out_15[5], 1'b1);
  xor xor_15 (xor_9_out[6], out_15[6], 1'b1);
  xor xor_16 (xor_9_out[7], out_15[7], 1'b1);
  xor xor_17 (xor_9_out[8], out_15[8], 1'b1);
  xor xor_18 (xor_9_out[9], out_15[9], 1'b1);
  xor xor_19 (xor_9_out[10], out_15[10], 1'b1);
  xor xor_20 (xor_9_out[11], out_15[11], 1'b1);

  assign out_20[10:0] = out_19[10:0];

  // Notes on the sheet:
  //   Sign(A)
  //   Exponent(A)
  //   Fraction(A)
  //   Sign(B)
  //   Exponent(B)
  //   Fraction(B)
endmodule
