// Logisim project Register file.circ as structural Verilog
module Register_File (
  input  [7:0] Write_Data,
  input  [3:0] Read_Reg1,
  input  [3:0] Read_Reg2,
  input  [3:0] Write_Reg,
  input  Reg_clock,
  input  RegWrite,
  output [7:0] Read_Data_1,
  output [7:0] Read_Data_2,
  output Error_Write_to_0
);

  wire and_2_out, and_3_out, and_4_out, and_5_out, and_6_out, and_7_out, and_8_out, decoder_1_out0,
       decoder_1_out1, decoder_1_out2, decoder_1_out3, decoder_1_out4, decoder_1_out5, decoder_1_out6,
       decoder_1_out7;
  wire [7:0] register_1_q, register_2_q, register_3_q, register_4_q, register_5_q, register_6_q,
       register_7_q, register_8_q;

  Decoder #(.select(4), .enable("false")) decoder_1 (
    .out0(decoder_1_out0), .out1(decoder_1_out1), .out2(decoder_1_out2), .out3(decoder_1_out3),
    .out4(decoder_1_out4), .out5(decoder_1_out5), .out6(decoder_1_out6), .out7(decoder_1_out7),
    .sel(Write_Reg));  // open: out8, out9, out10, out11, out12, out13, out14, out15
  and and_1 (Error_Write_to_0, decoder_1_out0, RegWrite);
  and and_2 (and_2_out, decoder_1_out1, RegWrite);
  and and_3 (and_3_out, decoder_1_out2, RegWrite);
  and and_4 (and_4_out, decoder_1_out3, RegWrite);
  and and_5 (and_5_out, decoder_1_out4, RegWrite);
  and and_6 (and_6_out, decoder_1_out5, RegWrite);
  and and_7 (and_7_out, decoder_1_out6, RegWrite);
  and and_8 (and_8_out, decoder_1_out7, RegWrite);
  Register #(.trigger("falling")) register_1 (.D(Write_Data), .Q(register_1_q));  // open: en, clk, clr
  Register #(.trigger("falling")) register_2 (
    .D(Write_Data), .en(and_2_out), .Q(register_2_q), .clk(Reg_clock));  // open: clr
  Register #(.trigger("falling")) register_3 (
    .D(Write_Data), .en(and_3_out), .Q(register_3_q), .clk(Reg_clock));  // open: clr
  Register #(.trigger("falling")) register_4 (
    .D(Write_Data), .en(and_4_out), .Q(register_4_q), .clk(Reg_clock));  // open: clr
  Register #(.trigger("falling")) register_5 (
    .D(Write_Data), .en(and_5_out), .Q(register_5_q), .clk(Reg_clock));  // open: clr
  Register #(.trigger("falling")) register_6 (
    .D(Write_Data), .en(and_6_out), .Q(register_6_q), .clk(Reg_clock));  // open: clr
  Register #(.trigger("falling")) register_7 (
    .D(Write_Data), .en(and_7_out), .Q(register_7_q), .clk(Reg_clock));  // open: clr
  Register #(.trigger("falling")) register_8 (
    .D(Write_Data), .en(and_8_out), .Q(register_8_q), .clk(Reg_clock));  // open: clr
  Multiplexer #(.select(4), .width(8), .enable("false")) multiplexer_1 (
    .in0(register_1_q), .in1(register_2_q), .in2(register_3_q), .in3(register_4_q), .in4(register_5_q),
    .in5(register_6_q), .in6(register_7_q), .in7(register_8_q), .out(Read_Data_1), .sel(Read_Reg1));  // open: in8, in9, in10, in11, in12, in13, in14, in15
  Multiplexer #(.select(4), .width(8), .enable("false")) multiplexer_2 (
    .in0(register_1_q), .in1(register_2_q), .in2(register_3_q), .in3(register_4_q), .in4(register_5_q),
    .in5(register_6_q), .in6(register_7_q), .in7(register_8_q), .in8(register_8_q), .out(Read_Data_2),
    .sel(Read_Reg2));  // open: in9, in10, in11, in12, in13, in14, in15
endmodule
