// Logisim project Pipelining.circ as structural Verilog: 1 circuit, main circuit main
module main (
  input  Reg_INIT,
  input  Reg_INIT_clock,
  input  [3:0] Reg_INIT_num,
  input  [7:0] Reg_INIT_data
);

  wire clock_1_out;
  wire [1:0] register_4_q, register_8_q;
  wire [2:0] register_3_q;
  wire [3:0] register_7_q, register_11_q, register_13_q;
  wire [7:0] adder_1_out, alu_1_f, multiplexer_1_out, multiplexer_2_out, register_1_q, register_5_q,
       register_6_q, register_9_q, register_10_q, register_12_q, register_file_1_read_data_1,
       register_file_1_read_data_2;
  wire [11:0] rom_2_data;
  wire [19:0] register_2_q, rom_1_data;

  Clock clock_1 (.out(clock_1_out));
  Register register_1 (.D(adder_1_out), .Q(register_1_q), .clk(clock_1_out));  // open: en, clr
  Adder adder_1 (.a(8'h1), .b(register_1_q), .out(adder_1_out));  // open: cin, cout
  ROM #(.dataWidth(20)) rom_1 (.addr(register_1_q), .data(rom_1_data));  // open: sel
  Register #(.width(20)) register_2 (.D(rom_1_data), .Q(register_2_q), .clk(clock_1_out));  // open: en, clr
  ROM #(.addrWidth(4), .dataWidth(12)) rom_2 (.addr(register_2_q[19:16]), .data(rom_2_data));  // open: sel
  Register_File register_file_1 (
    .Write_Data(register_12_q), .Init_tWrite_Data(Reg_INIT_data), .Read_Reg1(register_2_q[15:12]),
    .Read_Reg2(register_2_q[11:8]), .Write_Reg(register_13_q), .init_Write_Reg(Reg_INIT_num),
    .Reg_clock(clock_1_out), .Init_Reg_clock(Reg_INIT_clock), .reg_init(Reg_INIT), .RegWrite(rom_2_data[8]),
    .Read_Data_1(register_file_1_read_data_1), .Read_Data_2(register_file_1_read_data_2));  // open: Error_Write_to_0
  Register #(.width(3)) register_3 (.D(rom_2_data[2:0]), .Q(register_3_q), .clk(clock_1_out));  // open: en, clr
  Register #(.width(2)) register_4 (.D(rom_2_data[7:6]), .Q(register_4_q), .clk(clock_1_out));  // open: en, clr
  Register register_5 (.D(register_file_1_read_data_1), .Q(register_5_q), .clk(clock_1_out));  // open: en, clr
  Register register_6 (.D(register_file_1_read_data_2), .Q(register_6_q), .clk(clock_1_out));  // open: en, clr
  Register #(.width(4)) register_7 (.D(register_2_q[7:4]), .Q(register_7_q), .clk(clock_1_out));  // open: en, clr
  Multiplexer #(.select(2), .width(8), .enable("false")) multiplexer_1 (
    .in0(register_5_q), .in1(register_12_q), .in2(register_9_q), .out(multiplexer_1_out));  // open: in3, sel
  Multiplexer #(.select(2), .width(8), .enable("false")) multiplexer_2 (
    .in0(register_6_q), .in1(register_12_q), .in2(register_9_q), .out(multiplexer_2_out));  // open: in3, sel
  ALU alu_1 (
    .A(multiplexer_1_out), .B(multiplexer_2_out), .ALUop(register_3_q), .F(alu_1_f));  // open: overflow, negative, ZF
  Register #(.width(2)) register_8 (.D(register_4_q), .Q(register_8_q), .clk(clock_1_out));  // open: en, clr
  Register register_9 (.D(alu_1_f), .Q(register_9_q), .clk(clock_1_out));  // open: en, clr
  Register register_10 (.D(register_6_q), .Q(register_10_q), .clk(clock_1_out));  // open: en, clr
  Register #(.width(4)) register_11 (.D(register_7_q), .Q(register_11_q), .clk(clock_1_out));  // open: en, clr
  RAM #(.bus("separate")) ram_1 (
    .addr(register_9_q), .din(register_10_q), .str(register_8_q[0]), .clk(clock_1_out), .ld(register_8_q[1]));  // open: data, sel, clr
  Register register_12 (.D(register_9_q), .Q(register_12_q), .clk(clock_1_out));  // open: en, clr
  Register #(.width(4)) register_13 (.D(register_11_q), .Q(register_13_q), .clk(clock_1_out));  // open: en, clr

  // Notes on the sheet:
  //   contents of rom_1 (hex, n*v repeats v):
  //   777ff 43420 d3510 62150 f3420 54420 32a e0542 832fc 732f6 b32f6 332f6 932fc a530a 97200 87701 76203
  //   97600 87701 a7300 77701 23200 114f0 c0000 c0700 c1600
  //   IF/ID
  //   contents of rom_2 (hex, n*v repeats v):
  //   f05 31 21 302 500 504 503 300 301 240 380 303 f 501 f06 502
  //   RegWrite
  //   ID/EX
  //   ALUOp
  //   Forwarding Unit
  //   4 input
  //   2 output
  //   EX/MEM
  //   MemWrite
  //   MemRead
  //   MEM/WB
endmodule
